// Logisim project DL LAB 6.circ as structural Verilog: 1 circuit, main circuit main
module main (
  input  in_1,
  input  in_2,
  input  in_3,
  input  in_4,
  input  in_5,
  input  in_6,
  output out_7
);

  wire and_9_out, and_10_out, not_1_out, not_3_out, not_4_out, not_5_out, not_6_out;

  not not_1 (not_1_out, in_1);
  not not_2 (not_1_out, in_2);
  not not_3 (not_3_out, in_3);
  not not_4 (not_4_out, in_4);
  // AND_Gate and_1 has open pins: in0=not_1_out, in1=not_1_out, in2=not_3_out, in3=not_4_out, out=open
  // AND_Gate and_2 has open pins: in0=not_1_out, in1=not_1_out, in2=in_3, in3=not_4_out, out=open
  // AND_Gate and_3 has open pins: in0=not_1_out, in1=in_2, in2=not_3_out, in3=in_4, out=open
  // AND_Gate and_4 has open pins: in0=not_1_out, in1=in_2, in2=in_3, in3=in_4, out=open
  // AND_Gate and_5 has open pins: in0=in_1, in1=not_1_out, in2=not_3_out, in3=not_4_out, out=open
  // AND_Gate and_6 has open pins: in0=in_1, in1=not_1_out, in2=in_3, in3=not_4_out, out=open
  // AND_Gate and_7 has open pins: in0=in_1, in1=in_2, in2=not_3_out, in3=in_4, out=open
  // AND_Gate and_8 has open pins: in0=in_1, in1=in_2, in2=in_3, in3=in_4, out=open
  not not_5 (not_5_out, in_5);
  not not_6 (not_6_out, in_6);
  and and_9 (and_9_out, not_5_out, not_6_out);
  and and_10 (and_10_out, in_5, in_6);
  or or_1 (out_7, and_9_out, and_10_out);
endmodule
