// Logisim project DL LAB.circ.1.circ as structural Verilog: 1 circuit, main circuit main
module main (
  input  A,
  input  B,
  input  A_2,
  input  B_2,
  input  A_3,
  input  A_4,
  input  B_3,
  input  A_5,
  input  B_4,
  output Y,
  output Y_2,
  output Y_3,
  output Y_4,
  output Y_5
);

  and and_1 (Y, A, B);
  or or_1 (Y_2, A_2, B_2);
  not not_1 (Y_3, A_3);
  xor xor_1 (Y_4, A_4, B_3);
  xnor xnor_1 (Y_5, A_5, B_4);
endmodule
