// Logisim project DL LAB 9.circ as structural Verilog: 1 circuit, main circuit main
module main (
  input  in_1,
  input  in_2,
  output Difference,
  output Barrow
);

  wire not_1_out;

  not not_1 (not_1_out, in_2);
  xor xor_1 (Difference, in_1, in_2);
  and and_1 (Barrow, not_1_out, in_2);
endmodule
