// Logisim project dl.circ as structural Verilog: 1 circuit, main circuit main
module main (
  input  in_1,
  input  in_2,
  input  in_3,
  input  in_4,
  input  in_5,
  input  in_6,
  input  in_7,
  input  in_8,
  output out_9,
  output out_10,
  output out_11,
  output out_12
);

  wire and_1_out, not_3_out, not_4_out, not_5_out, not_6_out, or_1_out;

  or or_1 (or_1_out, in_1, in_3);
  and and_1 (and_1_out, in_6, in_7);
  not not_1 (out_9, or_1_out);
  not not_2 (out_12, and_1_out);
  not not_3 (not_3_out, in_2);
  not not_4 (not_4_out, in_4);
  not not_5 (not_5_out, in_5);
  not not_6 (not_6_out, in_8);
  and and_2 (out_10, not_3_out, not_4_out);
  or or_2 (out_11, not_5_out, not_6_out);

  // Notes on the sheet:
  //   in_3: pull=down
  //   in_4: pull=down
endmodule
